# Fritzing sketch wire diagram (saved by Fritzing 0.9.3b)
breadboards: 1

parts:
  Part1 = Arduino Uno (Rev3)
  J1 = Basic Servo
  J2 = Basic Servo
  S1 = Pololu QTR-8 Reflectabce Sensor array [package=THT]

nets:
  N1: Part1.D8, S1.pin4, S1.pin6
  N2: Part1.D9_PWM, S1.pin3, S1.pin5
  N3: Part1.D12/MISO, J2.pulse
  N4: Part1.D13/SCK, J1.pulse
  N5: Part1.D2, S1.pin12
  N6: Part1.D3_PWM, S1.pin11
  N7: Part1.D4, S1.pin10
  N8: Part1.D5_PWM, S1.pin9
  N9: Part1.D6_PWM, S1.pin8
  N10: Part1.D7, S1.pin7
  VCC: Part1.5V, J1.vcc, J2.vcc, S1.pin2, S1.pin14, S1.pin22
  GND: Part1.GND, J1.gnd, J2.gnd, S1.pin1, S1.pin15, S1.pin21
